# Fritzing sketch C86_Circuit (saved by Fritzing 0.9.0b)
breadboards: 3

parts:
  R4 = Resistor [tolerance=±5% resistance=4.7k package=THT]  # not connected
  R5 = Resistor [tolerance=±5% resistance=4.7k package=THT]
  C3 = Ceramic Capacitor [capacitance=100nF package="100 mil [THT, multilayer]"]
  R6 = Resistor [tolerance=±5% resistance=1k package=THT]
  C4 = Ceramic Capacitor [capacitance=47nF package="100 mil [THT, multilayer]"]
  パーツ4 = Audio Jack Breakout
  パーツ6 = Arduino Mega ADK (Rev3)
  IC2 = IC, DIP package, 28 pins [chip_label="AquesTalk ATP3011F4"]
  パーツ8 = Barometric Pressure Sensor - BMP085 Breakout
  パーツ9 = Barometric Pressure Sensor - BMP085 Breakout
  パーツ11 = SO-28W [chip_label=SO-24W package=SO-28W]
  パーツ12 = SO-28W [chip_label=SO-24W package=SO-28W]
  BAT5 = Battery Holders [package=battery_20mm_pth_compact]  # not connected
  S2 = Pushbutton [package="[SMD]"]
  IC5 = IC, DIP package, 8 pins [chip_label=SIS-2]
  Q3 = TRANSISTOR_NPN [package=to-92]
  R7 = Resistor [tolerance=±5% resistance=220 package=THT]

nets:
  N1: R5.Pin_0, パーツ6.D20/SDA, IC2.pin27, パーツ9.GND
  N2: C3.0, IC2.pin7, IC2.pin20, パーツ8.VCC, IC5.pin1, IC5.pin4, IC5.pin7, IC5.pin8, Q3.C
  GND: C3.1, C4.0, パーツ4.GND, IC2.pin4, IC2.pin8, IC2.pin22, パーツ8.GND, パーツ9.XCLR, IC5.pin6, Q3.B, R7.Pin_0, R7.Pin_1
  N3: R6.Pin_0, IC2.pin12
  N4: R6.Pin_1, C4.1, パーツ4.TIP
  N5: パーツ6.A8, IC5.pin2
  N6: パーツ6.A9, IC5.pin3
  N7: パーツ6.D21/SCL, IC2.pin28, パーツ9.EOC
  N8: パーツ6.D17/RX2, パーツ8.EOC
  N9: パーツ6.D16/TX2, パーツ8.XCLR
  N10: パーツ6.RESET, IC2.pin1
  N11: パーツ6.3V3, パーツ9.SCL, パーツ11.22, パーツ11.23, パーツ11.24, パーツ11.25, パーツ11.28
  N12: パーツ6.GND, パーツ11.1
  N13: パーツ6.D22, パーツ11.5
  N14: パーツ8.SCL, パーツ8.SDA
  N15: パーツ12.1, パーツ12.13, S2.Pin_3, S2.Pin_4
  N16: パーツ12.15, S2.Pin_1, S2.Pin_2
  N17: パーツ12.22, パーツ12.23, パーツ12.24, パーツ12.25, パーツ12.28
  N18: IC5.pin5, Q3.E

custom parts:
  Barometric Pressure Sensor - BMP085 Breakout: Description: This is a simple breakout board for the BMP085 high-precision, low-power barometric pressure sensor. The BMP085 offers a measuring range of 300 to 1100 hPa with an absolute accuracy of down to 0.03 hPa. It's based on piezo-resistive technology for EMC robustness, high accuracy and linearity as well as long term stability. This sensor supports a voltage supply between 1.8 and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
  Barometric Pressure Sensor - BMP085 Breakout: Description: This is a simple breakout board for the BMP085 high-precision, low-power barometric pressure sensor. The BMP085 offers a measuring range of 300 to 1100 hPa with an absolute accuracy of down to 0.03 hPa. It's based on piezo-resistive technology for EMC robustness, high accuracy and linearity as well as long term stability. This sensor supports a voltage supply between 1.8 and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
